# Fritzing sketch LCD (saved by Fritzing 0.9.2b)
breadboards: 1

parts:
  LCD1 = LCD screen  # not connected
  J1 = female pin header, 16 pins [form="♀ (female)"]
  Parte1 = Arduino Uno (Rev3)
  R1 = Trimmer Potentiometer [maximum_resistance=10kΩ package=THT]
  S1 = Pushbutton [package="[THT]"]

nets:
  N1: J1.pin1, Parte1.D12/MISO
  N2: J1.pin2, Parte1.D11_PWM/MOSI
  N3: J1.pin3, Parte1.D10_PWM/SS
  N4: J1.pin4, Parte1.D9_PWM
  N5: J1.pin9, Parte1.D8
  N6: J1.pin10, J1.pin14, J1.pin15, Parte1.GND, R1.leg2
  N7: J1.pin11, Parte1.D7
  N8: J1.pin12, R1.wiper
  N9: J1.pin13, Parte1.5V, R1.leg1, S1.Pin_1, S1.Pin_2
  N10: J1.pin16, S1.Pin_3, S1.Pin_4
