# Fritzing sketch Sensores_Vincios (saved by Fritzing 0.9.2b)
breadboards: 3

parts:
  Parte1 = Arduino Uno (Rev3)
  T1 = LM35 Temperature Sensor [package="TO92 [THT]"]
  R1 = Photocell (LDR) [package=THT]
  R2 = Resistor [tolerance=±5% resistance=220 package=THT]
  J1 = female pin header, 3 pins [form="♀ (female)"]
  Parte2 = HUZZAH ESP8266 Breakout  # not connected
  LED1 = LED - 5mm [color="Orange (620nm)" package="5 mm [THT]"]
  R3 = Resistor [tolerance=±5% resistance=220 package=THT]
  LED2 = LED - 5mm [color="Green (570nm)" package="5 mm [THT]"]
  R4 = Resistor [tolerance=±5% resistance=220 package=THT]
  LED3 = LED - 5mm [color="Blue (525nm)" package="5 mm [THT]"]
  R5 = Resistor [tolerance=±5% resistance=220 package=THT]

nets:
  N1: Parte1.A0, T1.Vout
  N2: Parte1.A1, R1.pin_0, R2.Pin_1
  N3: Parte1.A2, J1.pin2
  N4: Parte1.D2, LED1.anode
  N5: Parte1.D3_PWM, LED2.anode
  N6: Parte1.D4, LED3.anode
  N7: Parte1.5V, T1.+Vs, R1.pin_1, J1.pin1
  GND: Parte1.GND, T1.GND, R2.Pin_0, J1.pin3
  N8: LED1.cathode, R3.Pin_1
  N9: R3.Pin_0, R4.Pin_0, R5.Pin_0
  N10: LED2.cathode, R4.Pin_1
  N11: LED3.cathode, R5.Pin_1

notes:
  Sensor de humedad
  Sensor de luminosidad
  Sensor de temperatura
  Huzzah ESP8266
  Arduino UNO
  Consultar LCD.pdf para las conexiones de la pantalla.
  Rx (ESP8266) → Tx (Arduino)
  Tx (ESP8266) → Rx (Arduino)

custom parts:
  HUZZAH ESP8266 Breakout: The ESP8266 processor from Espressif is an 80 MHz microcontroller with a full WiFi front-end (both as client and access point) and TCP/IP stack with DNS support as well.

// code stored in the sketch: Sensores_Vincios.ino
#include <LiquidCrystal.h>

LiquidCrystal lcd(7, 8, 9, 10, 11, 12);

int orange_led =  2;
int green_led = 3;
int blue_led = 4;

float temp = 0;
int lum = 0;
int humid = 0;

unsigned long millis_ts = 0;
unsigned long interval_ts = 60000; // thingspeak interval

unsigned long millis_lcd = 0;
int interval_lcd = 5000; // lcd interval

int page_lcd = 0;

void setup() {
  pinMode(orange_led, OUTPUT);
  pinMode(green_led, OUTPUT);
  pinMode(blue_led, OUTPUT);

  digitalWrite(orange_led, HIGH);
  digitalWrite(green_led, HIGH);
  digitalWrite(blue_led, HIGH);

  Serial.begin(9600);

  lcd.begin(16, 2);
  lcd.print("CEIP Vincios");
}

void loop() {
  temp = analogRead(A0)*0.488;
  lum = map(analogRead(A1), 0, 1023, 100, 0);
  humid = map(analogRead(A2), 0, 1023, 100, 0);

  if (humid < 33) {
    digitalWrite(orange_led, HIGH);
    digitalWrite(green_led, LOW);
    digitalWrite(blue_led, LOW);
  } else if (humid >= 33 && humid < 66) {
    digitalWrite(orange_led, LOW);
    digitalWrite(green_led, HIGH);
    digitalWrite(blue_led, LOW);
  } else {
    digitalWrite(orange_led, LOW);
    digitalWrite(green_led, LOW);
    digitalWrite(blue_led, HIGH);
  }
  
  unsigned long millis_current = millis();

  if (millis_current - millis_lcd >= interval_lcd) {
    millis_lcd = millis_current;   
    lcd.clear();
    if (page_lcd > 2) page_lcd = 0;

    if (page_lcd == 0) {
      lcd.print("TEMPERATURA");
      lcd.setCursor(0,1);
      lcd.print(round(temp));
      lcd.print(" ");
      lcd.print(char(223));
      lcd.print("C");
    } else if (page_lcd == 1) {
      lcd.print("LUMINOSIDADE");
      lcd.setCursor(0,1);
      lcd.print(lum);
      lcd.print(" %");
    } else {
      lcd.print("HUMIDADE");
      lcd.setCursor(0,1);
      lcd.print(humid);
      lcd.print(" %");
    }

    page_lcd++;
  }
 
  if (millis_current - millis_ts >= interval_ts) {
    millis_ts = millis_current;   

    Serial.print("field1=");
    Serial.print(temp);
    Serial.print("&field2=");
    Serial.print(lum);
    Serial.print("&field3=");
    Serial.println(humid);
  }
}
